// Logisim project counter.circ as structural Verilog: 2 circuits, main circuit main
module main (
  input  R,
  input  C,
  input  T,
  output d0,
  output d1,
  output d2,
  output d3,
  output d4
);

  wire and_1_out, clock_1_out, nor_1_out, or_1_out;

  and and_1 (and_1_out, C, T);
  or or_1 (or_1_out, nor_1_out, R);
  JKRS_Trigger jkrs_trigger_1 (.J(1'b1), .C(and_1_out), .K(1'b1), .R(or_1_out), .Q(d0));  // open: S, notQ
  nor nor_1 (nor_1_out, d0, d1, d2, d3, d4);
  Clock clock_1 (.out(clock_1_out));
  // Digital_Oscilloscope Time_diagram: pin names not known; wires that end beside it: clock_1_out, R, T, d0, d1, d2, d3, d4, C
  JKRS_Trigger jkrs_trigger_2 (.J(1'b1), .C(d0), .K(1'b1), .R(or_1_out), .Q(d1));  // open: S, notQ
  JKRS_Trigger jkrs_trigger_3 (.J(1'b1), .C(d1), .K(1'b1), .R(or_1_out), .Q(d2));  // open: S, notQ
  JKRS_Trigger jkrs_trigger_4 (.S(or_1_out), .J(1'b1), .C(d2), .K(1'b1), .Q(d3));  // open: R, notQ
  JKRS_Trigger jkrs_trigger_5 (.S(or_1_out), .J(1'b1), .C(d3), .K(1'b1), .Q(d4));  // open: R, notQ
endmodule

module JKRS_Trigger (
  input  S,
  input  J,
  input  C,
  input  K,
  input  R,
  output Q,
  output notQ
);

  wire nand_1_out, nand_2_out, nand_3_out, nand_4_out, nand_5_out, nand_6_out, not_1_out, not_2_out,
       not_3_out;

  not not_1 (not_1_out, S);
  not not_2 (not_2_out, C);
  not not_3 (not_3_out, R);
  nand nand_1 (nand_1_out, not_1_out, notQ, J, not_2_out);
  nand nand_2 (nand_2_out, not_2_out, K, Q, not_3_out);
  nand nand_3 (nand_3_out, not_1_out, nand_1_out, nand_4_out);
  nand nand_4 (nand_4_out, nand_3_out, nand_2_out, not_3_out);
  nand nand_5 (nand_5_out, nand_1_out, nand_3_out);
  nand nand_6 (nand_6_out, nand_4_out, nand_2_out);
  nand nand_7 (Q, not_1_out, nand_5_out, notQ);
  nand nand_8 (notQ, Q, nand_6_out, not_3_out);
endmodule
