// Logisim project lfsr.circ as structural Verilog: 2 circuits, main circuit D_Trigger
module D_Trigger (
  input  S,
  input  C,
  input  D,
  input  R,
  output Q,
  output notQ
);

  wire nand_1_out, nand_2_out, nand_3_out, nand_4_out, not_1_out, not_2_out;

  not not_1 (not_1_out, S);
  not not_2 (not_2_out, R);
  nand nand_1 (nand_1_out, nand_4_out, not_1_out, nand_2_out);
  nand nand_2 (nand_2_out, nand_1_out, C, not_2_out);
  nand nand_3 (nand_3_out, nand_2_out, C, nand_4_out);
  nand nand_4 (nand_4_out, nand_3_out, D, not_2_out);
  nand nand_5 (Q, not_1_out, nand_2_out, notQ);
  nand nand_6 (notQ, Q, nand_3_out, not_2_out);
endmodule

module lfsrg_galois_myD (
  input  Set1,
  input  T,
  output d0,
  output d1,
  output d2,
  output d3,
  output d4,
  output d5,
  output d6,
  output d7
);

  wire xor_1_out, xor_2_out, xor_3_out, xor_4_out;

  D_Trigger d_trigger_1 (.S(Set1), .C(T), .D(d7), .Q(d0));  // open: R, notQ
  D_Trigger d_trigger_2 (.S(Set1), .C(T), .D(d0), .Q(d1));  // open: R, notQ
  D_Trigger d_trigger_3 (.S(Set1), .C(T), .D(d1), .Q(d2));  // open: R, notQ
  xor xor_1 (xor_1_out, d2, d7);
  D_Trigger d_trigger_4 (.S(Set1), .C(T), .D(xor_1_out), .Q(d3));  // open: R, notQ
  xor xor_2 (xor_2_out, d3, d7);
  D_Trigger d_trigger_5 (.S(Set1), .C(T), .D(xor_2_out), .Q(d4));  // open: R, notQ
  D_Trigger d_trigger_6 (.S(Set1), .C(T), .D(d4), .Q(d5));  // open: R, notQ
  xor xor_3 (xor_3_out, d5, d7);
  D_Trigger d_trigger_7 (.S(Set1), .C(T), .D(xor_3_out), .Q(d6));  // open: R, notQ
  xor xor_4 (xor_4_out, d6, d7);
  D_Trigger d_trigger_8 (.S(Set1), .C(T), .D(xor_4_out), .Q(d7));  // open: R, notQ
endmodule
